# Fritzing sketch DiagramaRobotEvitaObstaculos (saved by Fritzing 0.9.3b)
breadboards: 1

parts:
  R1 = Resistor [tolerance=±5% resistance=220 package=THT]
  C1 = Electrolytic Capacitor [capacitance=1µF package="100 mil [THT, electrolytic]"]
  S1 = H-Bridge with L298N
  Part1 = KY-012 Active Buzzer Module [package="Breakout board"]
  Componente1 = HC-SR04
  LED1 = RGB LED (com. cathode, rgb) [package="5 mm [THT]"]
  J1 = Basic Servo
  VCC1 = Battery
  VCC2 = Battery
  Componente2 = Arduino Uno (Rev3)
  M1 = DC Motor
  M2 = DC Motor

nets:
  GND: R1.Pin_0, C1.-, S1.GND, Part1.-, Componente1.Gnd, J1.gnd, VCC1.-, Componente2.GND
  N1: R1.Pin_1, LED1.common_cathode
  VCC: C1.+, Part1.+, Componente1.Vcc, Componente2.5V
  12V: S1.12V, VCC2.+, Componente2.VIN
  N2: S1.ENA, S1.ENA-5V
  N3: S1.IN1, Componente2.D6_PWM
  N4: S1.IN2, Componente2.D7
  N5: S1.IN3, Componente2.D8
  N6: S1.IN4, Componente2.D9_PWM
  N7: S1.ENB, S1.ENB-5V
  N8: S1.M1-01, M1.pin_2
  N9: S1.M1-02, M1.pin_1
  N10: S1.M2-01, M2.pin_2
  N11: S1.M2-02, M2.pin_1
  N12: Part1.S, Componente2.D3_PWM
  N13: Componente1.Trig, Componente2.D4
  N14: Componente1.Echo, Componente2.D5_PWM
  N15: LED1.red_anode, Componente2.A0
  N16: LED1.green_anode, Componente2.A1
  N17: LED1.blue_anode, Componente2.A2
  N18: J1.pulse, Componente2.D10_PWM/SS

custom parts:
  H-Bridge with L298N: h-bridge
  KY-012 Active Buzzer Module: Active Piezoelectric Buzzer Module Keyes KY-012, it produces single-tone sound when signal is high.
  HC-SR04: HC-SR04 ultrasonic distance sensor
