# Fritzing sketch DiagramaRobotEvitaObstaculosP1 (saved by Fritzing 0.9.3b)
breadboards: 1

parts:
  R1 = Resistor [tolerance=±5% resistance=220 package=THT]
  C1 = Electrolytic Capacitor [capacitance=1µF package="100 mil [THT, electrolytic]"]
  Part1 = KY-012 Active Buzzer Module [package="Breakout board"]
  Componente1 = HC-SR04
  LED1 = RGB LED (com. cathode, rgb) [package="5 mm [THT]"]
  Componente2 = Arduino Uno (Rev3)

nets:
  GND: R1.Pin_0, C1.-, Part1.-, Componente1.Gnd, Componente2.GND
  N1: R1.Pin_1, LED1.common_cathode
  VCC: C1.+, Part1.+, Componente1.Vcc, Componente2.5V
  N2: Part1.S, Componente2.D3_PWM
  N3: Componente1.Trig, Componente2.D4
  N4: Componente1.Echo, Componente2.D5_PWM
  N5: LED1.red_anode, Componente2.A0
  N6: LED1.green_anode, Componente2.A1
  N7: LED1.blue_anode, Componente2.A2

custom parts:
  KY-012 Active Buzzer Module: Active Piezoelectric Buzzer Module Keyes KY-012, it produces single-tone sound when signal is high.
  HC-SR04: HC-SR04 ultrasonic distance sensor
