# Fritzing sketch DiagramaRobotEvitaObstaculosP2 (saved by Fritzing 0.9.3b)
breadboards: 1

parts:
  Componente2 = Arduino Uno (Rev3)
  VCC1 = Battery
  VCC2 = Battery
  J1 = Basic Servo
  M1 = DC Motor
  M2 = DC Motor
  S1 = H-Bridge with L298N

nets:
  N1: Componente2.D8, S1.IN3
  N2: Componente2.D9_PWM, S1.IN4
  N3: Componente2.D10_PWM/SS, J1.pulse
  N4: Componente2.D6_PWM, S1.IN1
  N5: Componente2.D7, S1.IN2
  GND: Componente2.GND, VCC1.-, J1.gnd, S1.GND
  VIN: Componente2.VIN, VCC2.+, S1.12V
  N6: M1.pin_1, S1.M1-02
  N7: M1.pin_2, S1.M1-01
  N8: M2.pin_1, S1.M2-02
  N9: M2.pin_2, S1.M2-01
  N10: S1.ENA, S1.ENA-5V
  N11: S1.ENB, S1.ENB-5V

custom parts:
  H-Bridge with L298N: h-bridge
